# Fritzing sketch ESP32-TMC2130-4a (saved by Fritzing 0.9.3b)
circuit board: 10.0803cm x 6.27834cm
breadboards: 1

parts:
  U1 = ESP32-38PinWide [part_number=ESP32-38PinWide]
  D2 = Schottky Diode [part_number=1N5817 package="300 mil [THT]"]
  R1 = Resistor [tolerance=±5% resistance=510 package=THT]
  C6 = Tantalum Capacitor [capacitance=10µF package="200 mil [THT, tantalum]"]
  JTAG = Header 5x2 [package=avr_icsp]
  C5 = Tantalum Capacitor [capacitance="1 μF" package="200 mil [THT, tantalum]"]
  C7 = Tantalum Capacitor [capacitance=1μF package="100 mil [THT, tantalum]"]
  R2 = Resistor [tolerance=±5% resistance=39 package=THT]
  J8 = female pin header, 1 pin [form="♀ (female)"]
  S2 = female pin header, 1 pin [form="♀ (female)"]
  S3 = female pin header, 1 pin [form="♀ (female)"]  # not connected
  +12VDC = female pin header, 1 pin [form="♀ (female)"]
  JP2 = Header 5x2 [package=avr_icsp]
  J20 = female pin header, 3 pins [form="♀ (female)"]
  GND = female pin header, 1 pin [form="♀ (female)"]
  C8 = Tantalum Capacitor [capacitance=100nF package="200 mil [THT, tantalum]"]
  GND1 = female pin header, 1 pin [form="♀ (female)"]
  LM7805 = Voltage Regulator [package=78xxl]
  TMC2130 = SilentStepStick TMC2130 [package=SO16]
  IRLB8721 = MOSFET-NCHANNEL [package=to220v]
  C9 = Tantalum Capacitor [capacitance=1μF package="200 mil [THT, tantalum]"]

nets:
  N1: U1.3.3, D2.cathode
  N2: U1.EN, C7.+
  N3: U1.GPIO34, JP2.10
  N4: U1.GPIO35, JP2.8
  N5: U1.GPIO32, JP2.2
  N6: U1.GPIO33, JP2.5
  N7: U1.GPIO25, JP2.3
  N8: U1.GPIO26, JP2.1
  N9: U1.GPIO27, IRLB8721.G
  N10: U1.GPIO14, JTAG.2
  N11: U1.GPIO12, JTAG.8
  GND: U1.GND, C6.-, JTAG.3, JTAG.5, JTAG.7, JTAG.9, C5.-, C7.-, JP2.7, J20.pin3, GND.pin1, C8.-, GND1.pin1, LM7805.GND, TMC2130.DIR, TMC2130.GND, IRLB8721.S, C9.-
  N12: U1.GPIO13, JTAG.4
  5V: U1.VIN, C5.+, S2.pin1, LM7805.OUT, TMC2130.VIO, C9.+
  N13: U1.GPIO15, JTAG.6
  N14: U1.GPIO16, TMC2130.EN
  N15: U1.GPIO17, JP2.9, TMC2130.STEP
  N16: U1.GPIO5, TMC2130.CS
  N17: U1.GPIO18, TMC2130.SCK
  N18: U1.GPIO19, D2.anode, R1.Pin_0
  N19: U1.GPIO21, JP2.4
  N20: U1.GPIO3, J20.pin2
  N21: U1.GPIO1, J20.pin1
  N22: U1.GPIO22, JP2.6
  N23: U1.GPIO23, TMC2130.SDI
  N24: R1.Pin_1, TMC2130.SDO
  N25: C6.+, +12VDC.pin1, C8.+, LM7805.IN, TMC2130.VM
  N26: R2.Pin_0, IRLB8721.D
  N27: R2.Pin_1, J8.pin1

notes:
  +12V
  GND
  LEDs
  Serial I/O
  TX
  RX
  LED
  +5V
  motor
  +
  C7

custom parts:
  ESP32-38PinWide: Generic 38-Pin ESP32 with wide format (only access to one side of pins on a breadboard) based on Stephen Lilley's HiLetgo ESP-WROOM-32 ESP32 ESP-32S Development Board.
  SilentStepStick TMC2130: The TMC2130 (corrected by mke)
